# Fritzing sketch schematic (saved by Fritzing 0.9.3b)
breadboards: 1

parts:
  Part1 = Arduino Pro
  12V = DC Power [voltage=5]
  MOSFET = Basic FET N-Channel [package="TO220 [THT]"]
  Solenoid_Valve = Solenoid
  Schottky_Diode = Schottky Diode [part_number=1N5817 package="Melf DO-213 AB [SMD]"]
  R1 = Resistor [tolerance=±5% resistance=10k package=THT]
  5A_Fuse = FUSE [package=fuse_5mm]
  Override = Square Pushbutton
  Shower = LEDs [package=led10mm]
  Shower_2 = Square Pushbutton
  R3 = Resistor [tolerance=±5% resistance=150 package=THT]
  Stop = Square Pushbutton
  R4 = Resistor [tolerance=±5% resistance=150 package=THT]
  Stop_2 = LEDs [package=led10mm]
  NPN = TRANSISTOR_NPN_2 [package=to-92]
  Buzzer = Piezo Speaker
  R5 = Resistor [tolerance=±5% resistance=270 package=THT]

nets:
  N1: Part1.D2, MOSFET.gate, R1.Pin_0
  N2: Part1.D3_PWM, Shower_2.leg0
  N3: Part1.D4/A6, R3.Pin_1
  N4: Part1.D5_PWM, Stop.leg0
  N5: Part1.D6_PWM, R4.Pin_1
  N6: Part1.D7, Override.leg0
  N7: Part1.D8, R5.Pin_1
  N8: Part1.GND, 12V.V-, MOSFET.source, R1.Pin_1, Override.leg1, Shower.C, Shower_2.leg1, Stop.leg1, Stop_2.C, NPN.E
  N9: Part1.VCC, Solenoid_Valve.pin1, Schottky_Diode.cathode, 5A_Fuse.2
  N10: Part1.5V, Buzzer.pin1
  N11: 12V.V+, 5A_Fuse.1
  N12: MOSFET.drain, Solenoid_Valve.pin2, Schottky_Diode.anode
  N13: Shower.A, R3.Pin_0
  N14: R4.Pin_0, Stop_2.A
  N15: NPN.C, Buzzer.pin2
  N16: NPN.B, R5.Pin_0
